# Fritzing sketch Interfacing halleffect sensor with arduino (saved by Fritzing 0.9.9b)
breadboards: 1

parts:
  Part1 = Arduino Uno (Rev3)
  Mod1 = KY-024 Linear Hall Magnetic Sensor Module [package="Breakout board"]

nets:
  N1: Part1.D2, Mod1.G
  N2: Part1.5V, Mod1.D0
  N3: Part1.GND, Mod1.+

custom parts:
  KY-024 Linear Hall Magnetic Sensor Module: KY-024 Linear Hall Magnetic Sensor Module reacts iin the presence of a magnetic field.
